// Logisim project main.circ as structural Verilog: 8 circuits, main circuit main
module main (
  input  [3:0] A,
  input  [3:0] B,
  input  C,
  input  [2:0] S,
  output [3:0] out_5,
  output Cn_4,
  output OVR
);

  CI ci_1 (
    .A0(A[3]), .A1(A[2]), .A2(A[1]), .A3(A[0]), .B0(B[3]), .B1(B[2]), .B2(B[1]), .B3(B[0]), .Cn(C),
    .S0(S[2]), .S1(S[1]), .S2(S[0]), .F0(out_5[3]), .F1(out_5[2]), .F2(out_5[1]), .F3(out_5[0]), .Cn_4(Cn_4),
    .OVR(OVR));

  // Notes on the sheet:
  //   Unidade Lógica e Aritmética
endmodule

module CI (
  input  A0,
  input  A1,
  input  A2,
  input  A3,
  input  B0,
  input  B1,
  input  B2,
  input  B3,
  input  Cn,
  input  S0,
  input  S1,
  input  S2,
  output F0,
  output F1,
  output F2,
  output F3,
  output Cn_4,
  output OVR
);

  wire demultiplexer_1_out7, multiplexer_1_out, preset_1_out_9;

  CLEAR clear_1 (.A1(A0), .A2(A1), .A3(A2), .A4(A3));  // open: B1, B2, B3, B4, out_9
  XOR xor_1 ();  // open: A1, A2, A3, A4, B1, B2, B3, B4, out_9
  OR or_1 ();  // open: A1, A2, A3, A4, B1, B2, B3, B4, out_9
  AND and_1 ();  // open: A1, A2, A3, A4, B1, B2, B3, B4, out_9
  PRESET preset_1 (.A1(A0), .A2(A1), .A3(A2), .out_9(preset_1_out_9));  // open: A4, B1, B2, B3, B4
  Multiplexer #(.select(3)) multiplexer_1 (
    .in7(preset_1_out_9), .out(multiplexer_1_out), .sel({S2, S1, S0}));  // open: in0, in1, in2, in3, in4, in5, in6, en
  Demultiplexer #(.select(3)) demultiplexer_1 (
    .out7(demultiplexer_1_out7), .in(multiplexer_1_out), .sel({S2, S1, S0}));  // open: out0, out1, out2, out3, out4, out5, out6, en
  S_PRESET s_preset_1 (.in_1(demultiplexer_1_out7), .out_2(F0), .out_3(F1), .out_4(F2), .out_5(F3));

  // Notes on the sheet:
  //   A
  //   B
  //   C
  //   S
  //   F
  //   C
  //   OVR
endmodule

module AND (
  input  A1,
  input  A2,
  input  A3,
  input  A4,
  input  B1,
  input  B2,
  input  B3,
  input  B4,
  output out_9
);

  and and_1 (out_9, A1, A2, A3, A4, B1, B2, B3, B4);
endmodule

module OR (
  input  A1,
  input  A2,
  input  A3,
  input  A4,
  input  B1,
  input  B2,
  input  B3,
  input  B4,
  output out_9
);

  or or_1 (out_9, A1, A2, A3, A4, B1, B2, B3, B4);
endmodule

module XOR (
  input  A1,
  input  A2,
  input  A3,
  input  A4,
  input  B1,
  input  B2,
  input  B3,
  input  B4,
  output out_9
);

  ExactlyOne xor_1 (.out(out_9), .in0(A1), .in1(A2), .in2(A3), .in3(A4), .in4(B1), .in5(B2), .in6(B3), .in7(B4));
endmodule

module CLEAR (
  input  A1,
  input  A2,
  input  A3,
  input  A4,
  input  B1,
  input  B2,
  input  B3,
  input  B4,
  output out_9
);


  assign out_9 = 1'b0;
endmodule

module PRESET (
  input  A1,
  input  A2,
  input  A3,
  input  A4,
  input  B1,
  input  B2,
  input  B3,
  input  B4,
  output out_9
);


  assign out_9 = 1'b1;
endmodule

module S_PRESET (
  input  in_1,
  output out_2,
  output out_3,
  output out_4,
  output out_5
);


  assign out_2 = in_1;
  assign out_3 = in_1;
  assign out_4 = in_1;
  assign out_5 = in_1;
endmodule
